// Digital circuit 8-Bit-ALU.dig as structural Verilog
module _8_Bit_ALU (
  input  [7:0] A,
  input  [7:0] B,
  input  INVA,
  input  ENA,
  input  ENB,
  input  F0,
  input  F1,
  output carry_out,
  output [7:0] \output 
);

  wire alu_1_p10, alu_2_p10, alu_3_p10, alu_4_p10, alu_5_p10, alu_6_p10, alu_7_p10;

  // ALU alu_1: pin names not known; wires that end beside it: INVA, A[0], ENA, B[0], ENB, 1'b0, F0, F1, \output [0], alu_1_p10
  // ALU alu_2: pin names not known; wires that end beside it: INVA, A[1], ENA, B[1], ENB, alu_1_p10, F0, F1, \output [1], alu_2_p10
  // ALU alu_3: pin names not known; wires that end beside it: INVA, A[2], ENA, B[2], ENA, alu_2_p10, F0, F1, \output [2], alu_3_p10
  // ALU alu_4: pin names not known; wires that end beside it: INVA, A[3], ENA, B[3], ENB, alu_3_p10, F0, F1, \output [3], alu_4_p10
  // ALU alu_5: pin names not known; wires that end beside it: INVA, A[4], ENA, B[4], ENB, alu_4_p10, F0, F1, \output [4], alu_5_p10
  // ALU alu_6: pin names not known; wires that end beside it: INVA, A[5], ENA, B[5], ENB, alu_5_p10, F0, F1, \output [5], alu_6_p10
  // ALU alu_7: pin names not known; wires that end beside it: INVA, A[6], ENA, B[6], ENB, alu_6_p10, F0, F1, \output [6], alu_7_p10
  // ALU alu_8: pin names not known; wires that end beside it: INVA, A[7], ENA, B[7], ENB, alu_7_p10, F0, F1, \output [7], carry_out
endmodule
